# Fritzing sketch OLED_WITH_4844_schematic_atmega328 (saved by Fritzing 0.9.3b)
breadboards: 1

parts:
  part = OLED Monochrome 128x64 0.96 inch [part_number=.]
  S2 = SWITCH-MOMENTARY-2 [package=tactile-pth]
  S3 = SWITCH-MOMENTARY-2 [package=tactile-pth]
  S1 = SWITCH-MOMENTARY-2 [package=tactile-pth]
  part_2 = Arduino Pro Mini v13
  S4 = SWITCH-MOMENTARY-2 [package=tactile-pth]
  SI4844 = IC, DIP package, 24 pins [chip_label=IC]
  R7 = Resistor [tolerance=±5% resistance=10k package=THT]
  R8 = Resistor [tolerance=±5% resistance=10k package=THT]
  C1 = Capacitor [part_number=100nF package=cap-pth-small2]
  L1 = Inductor [part_number=AM package="1206 [SMD]"]
  C2 = Capacitor [part_number=470nF package=cap-pth-small2]
  ANT1 = Antenna [part_number=FM]
  L2 = Inductors [package=0603]
  R9 = Slide Potentiometer [maximum_resistance=100kΩ]
  R10 = Resistor [tolerance=±5% resistance=100 package=THT]
  C3 = Capacitor [part_number=4.7uF package=cap-pth-small2]
  C4 = Capacitor [part_number=4.7uF package=cap-pth-small2]

nets:
  N1: part.SCLK_SCK, part_2.A5, SI4844.pin17, R8.Pin_0
  N2: part.DC_SA0, part_2.A4, SI4844.pin16, R7.Pin_0
  3.3V: part.VIN, part_2.VCC, SI4844.pin20, SI4844.pin21, R7.Pin_1, R8.Pin_1, C1.2
  GND: part.GND, S2.1, S3.1, S1.1, part_2.GND, S4.1, SI4844.pin10, SI4844.pin14, L1.pin_1, R10.Pin_0
  N3: S2.2, part_2.D7
  N4: S3.2, part_2.D8
  N5: S1.2, part_2.D5_PWM
  D15 SI4844: part_2.D12/MISO
  N6: part_2.D6_PWM, S4.2
  D2 SI4844: part_2.D2
  D2 Arduino: SI4844.pin2
  N7: SI4844.pin3, R9.leg1
  N8: SI4844.pin4, R9.wiper
  N9: SI4844.pin8, ANT1.antenna_lead, L2.1
  N10: SI4844.pin9, SI4844.pin11
  N11: SI4844.pin12, C2.1
  D12 Arduino: SI4844.pin15
  N12: SI4844.pin22, C1.1
  N13: SI4844.pin23, C4.1
  N14: SI4844.pin24, C3.1
  N15: L1.pin_0, C2.2, L2.2
  N16: R9.leg2, R10.Pin_1
  Audio Left: C3.2
  Audio Right: C4.2

notes:
  Band
  OLED
  OLED, SI4844, Buttons and Arduino connection.
  Ricardo Lima Caratti - Oct, 2019
  SLC
  SDA
  D8
  D7
  D6
  D5
  Arduino D2 (Interrupt)
  SI4844 Pin 2 (Interrupt)
  BAND UP
  BAND DOWN
  VOLUME UP
  VOLUME DOWN

custom parts:
  OLED Monochrome 128x64 0.96 inch: These displays are small, only about 1" diameter, but very readable due to the high contrast of an OLED display. This display is made of 128x64 individual white OLED pixels, each one is turned on or off by the controller chip. Because the display makes its own light, no backlight is required. This reduces the power required to run the OLED and is why the display has such high contrast; we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
